# Fritzing sketch spring-meter-sketch (saved by Fritzing 0.9.3b)
breadboards: 1

parts:
  Part1 = Arduino Uno (Rev3) - ICSP
  U1 = LCD-16X2 [package=lcd-16x2_noholes]
  LCM1602_IIC2 = LCM1602 IIC [part_number="LCM1602 IIC" chip_label="LCM1602 IIC" package="DIP (Dual Inline) [THT]"]
  R1 = Resistor [tolerance=±5% resistance=10k package="0402 [SMD]"]
  R2 = Resistor [tolerance=±5% resistance=10k package="0402 [SMD]"]
  Part2 = Adafruit VL53L0X Time of Flight Distance Sensor [part_number="Adafruit #3317"]
  Part3 = HX711 Weighing Sensor Module  # not connected

nets:
  N1: Part1.A4/SDA, LCM1602_IIC2.SDA, R1.Pin_1, Part2.SDA
  N2: Part1.A5/SCL, LCM1602_IIC2.SCL, R2.Pin_0, Part2.SCL
  5V: Part1.5V, LCM1602_IIC2.VCC, R1.Pin_0, R2.Pin_1, Part2.VIN
  GND: Part1.GND, LCM1602_IIC2.GND, Part2.GND
  VSS: U1.VSS, LCM1602_IIC2.VSS
  VDD: U1.VDD, LCM1602_IIC2.VDD
  N3: U1.VO, LCM1602_IIC2.V0
  N4: U1.RS, LCM1602_IIC2.RS
  N5: U1.R_W, LCM1602_IIC2.RW
  N6: U1.E, LCM1602_IIC2.E
  N7: U1.DB0, LCM1602_IIC2.D0
  N8: U1.DB1, LCM1602_IIC2.D1
  N9: U1.DB2, LCM1602_IIC2.D2
  N10: U1.DB3, LCM1602_IIC2.D3
  N11: U1.DB4, LCM1602_IIC2.D4
  N12: U1.DB5, LCM1602_IIC2.D5
  N13: U1.DB6, LCM1602_IIC2.D6
  N14: U1.DB7, LCM1602_IIC2.D7
  N15: U1.A, LCM1602_IIC2.A
  N16: U1.K, LCM1602_IIC2.K

notes:
  SCL
  SDA
  Pull-up resistors (10k)

custom parts:
  LCM1602 IIC: I2C-Module to use a 1602 or 2004 LCD on with the wire.h libory Serial LCD Modul
  Adafruit VL53L0X Time of Flight Distance Sensor: The VL53L0X is a Time of Flight distance sensor like no other you've used! The sensor contains a very tiny invisible laser source, and a matching sensor. The VL53L0X can detect the "time of flight", or how long the light has taken to bounce back to the sensor. Since it uses a very narrow light source, it is good for determining distance of only the surface directly in front of it. Unlike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
